// Digital circuit P8D16A_2A main.dig as structural Verilog
module P8D16A_2A_main (
  input  CLK
);

  wire A_o0, A_o1, A_o2, A_o3, A_o4, A_o5, A_o6, A_o7, clock_1_clk, fumemory16_1_o0, fumemory16_1_o1,
       fumemory16_1_o2, fumemory16_1_o3, fumemory16_1_o4, fumemory16_1_o5, fumemory16_1_o6, fumemory16_1_o7,
       mareg16b_1_o0, mareg16b_1_o1, mareg16b_1_o2, mareg16b_1_o3, mareg16b_1_o4, mareg16b_1_o5,
       mareg16b_1_o6, mareg16b_1_o7, mareg16b_1_o8, mareg16b_1_o9, mareg16b_1_o10, mareg16b_1_o11,
       mareg16b_1_o12, mareg16b_1_o13, mareg16b_1_o14, mareg16b_1_o15, undriven, undriven_2, undriven_3,
       undriven_4, undriven_5, undriven_6, undriven_7, undriven_8, undriven_9, undriven_10, undriven_11,
       undriven_12, undriven_13, undriven_14, undriven_15, undriven_16, undriven_17, undriven_18,
       undriven_19, undriven_20, undriven_21, undriven_22, undriven_23, undriven_24, undriven_25,
       undriven_26, undriven_27, undriven_28, undriven_29, undriven_30, undriven_31, undriven_32,
       undriven_33, undriven_34;

  Register A (
    .CLK(undriven_26), .E(undriven_29), .R(undriven_32), .W(undriven_33), .D0(A_o0), .D1(A_o1), .D2(A_o2),
    .D3(A_o3), .D4(A_o4), .D5(A_o5), .D6(A_o6), .D7(A_o7), .O0(A_o0), .O1(A_o1), .O2(A_o2), .O3(A_o3),
    .O4(A_o4), .O5(A_o5), .O6(A_o6), .O7(A_o7));
  Register X (
    .CLK(undriven_34), .E(undriven_30), .R(undriven_28), .W(undriven_27), .D0(A_o0), .D1(A_o1), .D2(A_o2),
    .D3(A_o3), .D4(A_o4), .D5(A_o5), .D6(A_o6), .D7(A_o7), .O0(A_o0), .O1(A_o1), .O2(A_o2), .O3(A_o3),
    .O4(A_o4), .O5(A_o5), .O6(A_o6), .O7(A_o7));
  Clock clock_1 (.HLT(undriven_31), .Clock(CLK), .M_CLK(1'b0), .M_E(1'b0), .CLK(clock_1_clk));
  Register SP (
    .CLK(undriven_18), .E(undriven_21), .R(undriven_23), .W(undriven_24), .D0(A_o0), .D1(A_o1), .D2(A_o2),
    .D3(A_o3), .D4(A_o4), .D5(A_o5), .D6(A_o6), .D7(A_o7), .O0(A_o0), .O1(A_o1), .O2(A_o2), .O3(A_o3),
    .O4(A_o4), .O5(A_o5), .O6(A_o6), .O7(A_o7));
  Register Y (
    .CLK(undriven_25), .E(undriven_22), .R(undriven_20), .W(undriven_19), .D0(A_o0), .D1(A_o1), .D2(A_o2),
    .D3(A_o3), .D4(A_o4), .D5(A_o5), .D6(A_o6), .D7(A_o7), .O0(A_o0), .O1(A_o1), .O2(A_o2), .O3(A_o3),
    .O4(A_o4), .O5(A_o5), .O6(A_o6), .O7(A_o7));
  Reg16 O (
    .CLK(undriven_10), .E(undriven_8), .R(undriven_6), .W(undriven_4), .D0(undriven_3), .D1(undriven),
    .D2(A_o0), .D3(A_o1), .D4(A_o2), .D5(A_o3), .D6(A_o4), .D7(A_o5), .D8(A_o6), .D9(A_o7), .O0(A_o0),
    .O1(A_o1), .O2(A_o2), .O3(A_o3), .O4(A_o4), .O5(A_o5), .O6(A_o6), .O7(A_o7));  // open: D10, D11, D12, D13, D14, D15, O8, O9, O10, O11, O12, O13, O14, O15
  Register Z (
    .CLK(undriven_2), .E(undriven_5), .R(undriven_7), .W(undriven_9), .D0(A_o0), .D1(A_o1), .D2(A_o2),
    .D3(A_o3), .D4(A_o4), .D5(A_o5), .D6(A_o6), .D7(A_o7), .O0(A_o0), .O1(A_o1), .O2(A_o2), .O3(A_o3),
    .O4(A_o4), .O5(A_o5), .O6(A_o6), .O7(A_o7));
  ProgramCounter16 programcounter16_1 (
    .CLK(undriven_16), .E(undriven_15), .RL(undriven_14), .WL(undriven_13), .RH(undriven_12),
    .WH(undriven_11), .D0(A_o0), .D1(A_o1), .D2(A_o2), .D3(A_o3), .D4(A_o4), .D5(A_o5), .D6(A_o6), .D7(A_o7),
    .O0(A_o0), .O1(A_o1), .O2(A_o2), .O3(A_o3), .O4(A_o4), .O5(A_o5), .O6(A_o6), .O7(A_o7));
  Instruction_Decoder instruction_decoder_1 ();  // open: CLK, I0, I1, I2, I3, I4, I5, I6, I7, IRQ, INT, F0, FC, FO, FN, D0, D1, D2, D3, D4, D5, D6, D7, ALUE, ALU_B, ALUC, ALUADD, ALUAND, ALUOR, ALUNOT, ALUXOR, ALUSL, ALUSR, ALURL, ALURR, AR, AW, XR, XW, YR, YW, ZR, ZW, PCE, PCHR, PCHW, PCLR, PCLW, SPR, SPW, SPINC, SPDEC, LHR, LHW, LLR, LLW, MALW, MAHW, INTACK, HLT, TRR, MR, MW, TW, MAINC
  MAReg16b mareg16b_1 (
    .CLK(undriven_17), .D0(fumemory16_1_o0), .D1(fumemory16_1_o1), .D2(fumemory16_1_o2),
    .D3(fumemory16_1_o3), .D4(fumemory16_1_o4), .D5(fumemory16_1_o5), .D6(fumemory16_1_o6),
    .D7(fumemory16_1_o7), .O0(mareg16b_1_o0), .O1(mareg16b_1_o1), .O2(mareg16b_1_o2), .O3(mareg16b_1_o3),
    .O4(mareg16b_1_o4), .O5(mareg16b_1_o5), .O6(mareg16b_1_o6), .O7(mareg16b_1_o7), .O8(mareg16b_1_o8),
    .O9(mareg16b_1_o9), .O10(mareg16b_1_o10), .O11(mareg16b_1_o11), .O12(mareg16b_1_o12),
    .O13(mareg16b_1_o13), .O14(mareg16b_1_o14), .O15(mareg16b_1_o15));  // open: E, WL, WH
  FUMemory16 fumemory16_1 (
    .CLK(undriven_17), .A0(mareg16b_1_o0), .A1(mareg16b_1_o1), .A2(mareg16b_1_o2), .A3(mareg16b_1_o3),
    .A4(mareg16b_1_o4), .A5(mareg16b_1_o5), .A6(mareg16b_1_o6), .A7(mareg16b_1_o7), .A8(mareg16b_1_o8),
    .A9(mareg16b_1_o9), .A10(mareg16b_1_o10), .A11(mareg16b_1_o11), .A12(mareg16b_1_o12),
    .A13(mareg16b_1_o13), .A14(mareg16b_1_o14), .A15(mareg16b_1_o15), .D0(fumemory16_1_o0),
    .D1(fumemory16_1_o1), .D2(fumemory16_1_o2), .D3(fumemory16_1_o3), .D4(fumemory16_1_o4),
    .D5(fumemory16_1_o5), .D6(fumemory16_1_o6), .D7(fumemory16_1_o7), .O0(fumemory16_1_o0),
    .O1(fumemory16_1_o1), .O2(fumemory16_1_o2), .O3(fumemory16_1_o3), .O4(fumemory16_1_o4),
    .O5(fumemory16_1_o5), .O6(fumemory16_1_o6), .O7(fumemory16_1_o7));  // open: R, W, E
endmodule
