// Digital circuit ALU.dig as structural Verilog
module ALU (
  input  E,
  input  A0,
  input  A1,
  input  A2,
  input  A3,
  input  A4,
  input  A5,
  input  A6,
  input  A7,
  input  B0,
  input  B1,
  input  B2,
  input  B3,
  input  B4,
  input  B5,
  input  B6,
  input  B7,
  input  B,
  input  C,
  input  S,
  input  AND,
  input  ADD,
  input  OR,
  input  NOT,
  input  XOR,
  input  SL,
  input  SR,
  input  RL,
  input  RR,
  output O0,
  output O1,
  output O2,
  output O3,
  output O4,
  output O5,
  output O6,
  output O7,
  output F0,
  output FN,
  output FC,
  output FO
);

  wire adder8b_1_o1, adder8b_1_o2, adder8b_1_o3, adder8b_1_o4, adder8b_1_o5, adder8b_1_o6, adder8b_1_o7,
       and_1_out, not_1_out, not_2_out, not_3_out, not_4_out, not_5_out, not_6_out, not_7_out, not_8_out,
       xor_1_out, xor_2_out, xor_3_out, xor_4_out, xor_5_out, xor_6_out, xor_7_out, xor_8_out;

  xor xor_1 (xor_1_out, B7, B);
  xor xor_2 (xor_2_out, B6, B);
  xor xor_3 (xor_3_out, B5, B);
  xor xor_4 (xor_4_out, B3, B);
  xor xor_5 (xor_5_out, B4, B);
  xor xor_6 (xor_6_out, B2, B);
  xor xor_7 (xor_7_out, B1, B);
  xor xor_8 (xor_8_out, B0, B);
  Adder8b adder8b_1 (
    .E(ADD), .X0(A0), .X1(A1), .X2(A2), .X3(A3), .X4(A4), .X5(A5), .X6(A6), .X7(A7), .Y0(xor_8_out),
    .Y1(xor_7_out), .Y2(xor_6_out), .Y3(xor_4_out), .Y4(xor_5_out), .Y5(xor_3_out), .Y6(xor_2_out),
    .Y7(xor_1_out), .C(C), .S(S), .O0(FN), .O1(adder8b_1_o1), .O2(adder8b_1_o2), .O3(adder8b_1_o3),
    .O4(adder8b_1_o4), .O5(adder8b_1_o5), .O6(adder8b_1_o6), .O7(adder8b_1_o7), .CO(FC), .OO(FO));
  And8b and8b_1 (
    .E(AND), .X0(A0), .X1(A1), .X2(A2), .X3(A3), .X4(A4), .X5(A5), .X6(A6), .X7(A7), .Y0(xor_8_out),
    .Y1(xor_7_out), .Y2(xor_6_out), .Y3(xor_4_out), .Y4(xor_5_out), .Y5(xor_3_out), .Y6(xor_2_out),
    .Y7(xor_1_out), .O0(FN), .O1(adder8b_1_o1), .O2(adder8b_1_o2), .O3(adder8b_1_o3), .O4(adder8b_1_o4),
    .O5(adder8b_1_o5), .O6(adder8b_1_o6), .O7(adder8b_1_o7));
  Or8b or8b_1 (
    .E(OR), .X0(A0), .X1(A1), .X2(A2), .X3(A3), .X4(A4), .X5(A5), .X6(A6), .X7(A7), .Y0(xor_8_out),
    .Y1(xor_7_out), .Y2(xor_6_out), .Y3(xor_4_out), .Y4(xor_5_out), .Y5(xor_3_out), .Y6(xor_2_out),
    .Y7(xor_1_out), .O0(FN), .O1(adder8b_1_o1), .O2(adder8b_1_o2), .O3(adder8b_1_o3), .O4(adder8b_1_o4),
    .O5(adder8b_1_o5), .O6(adder8b_1_o6), .O7(adder8b_1_o7));
  Not8b not8b_1 (
    .E(NOT), .D0(A0), .D1(A1), .D2(A2), .D3(A3), .D4(A4), .D5(A5), .D6(A6), .D7(A7), .O0(FN),
    .O1(adder8b_1_o1), .O2(adder8b_1_o2), .O3(adder8b_1_o3), .O4(adder8b_1_o4), .O5(adder8b_1_o5),
    .O6(adder8b_1_o6), .O7(adder8b_1_o7));
  Xor8b xor8b_1 (
    .E(XOR), .X0(A0), .X1(A1), .X2(A2), .X3(A3), .X4(A4), .X5(A5), .X6(A6), .X7(A7), .Y0(xor_8_out),
    .Y1(xor_7_out), .Y2(xor_6_out), .Y3(xor_4_out), .Y4(xor_5_out), .Y5(xor_3_out), .Y6(xor_2_out),
    .Y7(xor_1_out), .O0(FN), .O1(adder8b_1_o1), .O2(adder8b_1_o2), .O3(adder8b_1_o3), .O4(adder8b_1_o4),
    .O5(adder8b_1_o5), .O6(adder8b_1_o6), .O7(adder8b_1_o7));
  ShiftLeft8b shiftleft8b_1 (
    .E(SL), .D0(A0), .D1(A1), .D2(A2), .D3(A3), .D4(A4), .D5(A5), .D6(A6), .D7(A7), .O0(FN),
    .O1(adder8b_1_o1), .O2(adder8b_1_o2), .O3(adder8b_1_o3), .O4(adder8b_1_o4), .O5(adder8b_1_o5),
    .O6(adder8b_1_o6), .O7(adder8b_1_o7), .C(FC));
  ShiftRight8b shiftright8b_1 (
    .E(SR), .D0(A0), .D1(A1), .D2(A2), .D3(A3), .D4(A4), .D5(A5), .D6(A6), .D7(A7), .O0(FN),
    .O1(adder8b_1_o1), .O2(adder8b_1_o2), .O3(adder8b_1_o3), .O4(adder8b_1_o4), .O5(adder8b_1_o5),
    .O6(adder8b_1_o6), .O7(adder8b_1_o7), .C(FC));
  // RotateLeft8b rotateleft8b_1: pin names not known; wires that end beside it: RL, A0, A1, A2, A3, A4, A5, A6, A7, FN, adder8b_1_o1, adder8b_1_o2, adder8b_1_o3, adder8b_1_o4, adder8b_1_o5, adder8b_1_o6, adder8b_1_o7, FC
  // RotateRight8b rotateright8b_1: pin names not known; wires that end beside it: xor_8_out, A7, A6, A5, A4, A3, A2, A1, A0, RR, A0, A1, A2, A3, A4, A5, A6, A7, FN, adder8b_1_o1, adder8b_1_o2, adder8b_1_o3, adder8b_1_o4, adder8b_1_o5, adder8b_1_o6, adder8b_1_o7, FC, FC, adder8b_1_o7, adder8b_1_o6, adder8b_1_o5, adder8b_1_o4, adder8b_1_o3, adder8b_1_o2, adder8b_1_o1, FN
  and and_1 (and_1_out, not_1_out, not_2_out, not_3_out, not_4_out);
  not not_1 (not_1_out, adder8b_1_o4);
  not not_2 (not_2_out, adder8b_1_o5);
  not not_3 (not_3_out, adder8b_1_o6);
  not not_4 (not_4_out, adder8b_1_o7);
  not not_5 (not_5_out, FN);
  not not_6 (not_6_out, adder8b_1_o1);
  not not_7 (not_7_out, adder8b_1_o2);
  not not_8 (not_8_out, adder8b_1_o3);
  and and_2 (F0, not_5_out, not_6_out, not_7_out, not_8_out, and_1_out);
  PinControl8b pincontrol8b_1 (
    .E(E), .D0(FN), .D1(adder8b_1_o1), .D2(adder8b_1_o2), .D3(adder8b_1_o3), .D4(adder8b_1_o4),
    .D5(adder8b_1_o5), .D6(adder8b_1_o6), .D7(adder8b_1_o7), .O0(O0), .O1(O1), .O2(O2), .O3(O3), .O4(O4),
    .O5(O5), .O6(O6), .O7(O7));

  // Notes on the sheet:
  //   C: Carry
endmodule
