// Digital circuit FUMemory16.dig as structural Verilog
module FUMemory16 (
  input  CLK,
  input  R,
  input  W,
  input  E,
  input  A0,
  input  A1,
  input  A2,
  input  A3,
  input  A4,
  input  A5,
  input  A6,
  input  A7,
  input  A8,
  input  A9,
  input  A10,
  input  A11,
  input  A12,
  input  A13,
  input  A14,
  input  A15,
  input  D0,
  input  D1,
  input  D2,
  input  D3,
  input  D4,
  input  D5,
  input  D6,
  input  D7,
  output O0,
  output O1,
  output O2,
  output O3,
  output O4,
  output O5,
  output O6,
  output O7
);

  wire and_1_out;

  and and_1 (and_1_out, CLK, E);
  EEPROMDualPort #(.AddrBits(16), .Bits(8)) eepromdualport_1 (
    .A({A15, A14, A13, A12, A11, A10, A9, A8, A7, A6, A5, A4, A3, A2, A1, A0}),
    .Din({D7, D6, D5, D4, D3, D2, D1, D0}), .str(W), .C(and_1_out), .ld(R),
    .D({O7, O6, O5, O4, O3, O2, O1, O0}));
endmodule
